# Fritzing sketch Schema (saved by Fritzing 0.9.5d)

parts:
  Raspberry_Pi_1 = Raspberry Pi 3 [part_number=RPI-3-V1.2]
  WeMos_D1_Mini_Relay_Shield_V1 = WeMos D1 Mini Relay Shield V2
  WeMos_D1_Mini_Relay_Shield_V3 = WeMos D1 Mini Relay Shield V2
  WeMos_D1_Mini_Relay_Shield_V4 = WeMos D1 Mini Relay Shield V2
  WeMos_D1_Mini_Relay_Shield_V2 = WeMos D1 Mini Relay Shield V2

nets:
  N1: Raspberry_Pi_1.GPIO19, WeMos_D1_Mini_Relay_Shield_V4.NC
  N2: Raspberry_Pi_1.GPIO26, WeMos_D1_Mini_Relay_Shield_V3.NC
  N3: Raspberry_Pi_1.GPIO21, WeMos_D1_Mini_Relay_Shield_V1.NC
  N4: Raspberry_Pi_1.GPIO20, WeMos_D1_Mini_Relay_Shield_V2.NC
